// Digital circuit Decoder.dig as structural Verilog
module Decoder (
  input  [6:0] In,
  output [27:0] Out2,
  output [63:0] Out1
);

  // IsEqual #(.generic("value := 91;")) isequal_1: pin names not known; wires that end beside it: In, Out2[27]
  // IsEqual #(.generic("value := 90;")) isequal_2: pin names not known; wires that end beside it: In, Out2[26]
  // IsEqual #(.generic("value := 89;")) isequal_3: pin names not known; wires that end beside it: In, Out2[25]
  // IsEqual #(.generic("value := 88;")) isequal_4: pin names not known; wires that end beside it: In, Out2[24]
  // IsEqual #(.generic("value := 87;")) isequal_5: pin names not known; wires that end beside it: In, Out2[23]
  // IsEqual #(.generic("value := 86;")) isequal_6: pin names not known; wires that end beside it: In, Out2[22]
  // IsEqual #(.generic("value := 85;")) isequal_7: pin names not known; wires that end beside it: In, Out2[21]
  // IsEqual #(.generic("value := 84;")) isequal_8: pin names not known; wires that end beside it: In, Out2[20]
  // IsEqual #(.generic("value := 83;")) isequal_9: pin names not known; wires that end beside it: In, Out2[19]
  // IsEqual #(.generic("value := 82;")) isequal_10: pin names not known; wires that end beside it: In, Out2[18]
  // IsEqual #(.generic("value := 81;")) isequal_11: pin names not known; wires that end beside it: In, Out2[17]
  // IsEqual #(.generic("value := 80;")) isequal_12: pin names not known; wires that end beside it: In, Out2[16]
  // IsEqual #(.generic("value := 79;")) isequal_13: pin names not known; wires that end beside it: In, Out2[15]
  // IsEqual #(.generic("value := 78;")) isequal_14: pin names not known; wires that end beside it: In, Out2[14]
  // IsEqual #(.generic("value := 77;")) isequal_15: pin names not known; wires that end beside it: In, Out2[13]
  // IsEqual #(.generic("value := 76;")) isequal_16: pin names not known; wires that end beside it: In, Out2[12]
  // IsEqual #(.generic("value := 75;")) isequal_17: pin names not known; wires that end beside it: In, Out2[11]
  // IsEqual #(.generic("value := 74;")) isequal_18: pin names not known; wires that end beside it: In, Out2[10]
  // IsEqual #(.generic("value := 73;")) isequal_19: pin names not known; wires that end beside it: In, Out2[9]
  // IsEqual #(.generic("value := 72;")) isequal_20: pin names not known; wires that end beside it: In, Out2[8]
  // IsEqual #(.generic("value := 71;")) isequal_21: pin names not known; wires that end beside it: In, Out2[7]
  // IsEqual #(.generic("value := 70;")) isequal_22: pin names not known; wires that end beside it: In, Out2[6]
  // IsEqual #(.generic("value := 69;")) isequal_23: pin names not known; wires that end beside it: In, Out2[5]
  // IsEqual #(.generic("value := 68;")) isequal_24: pin names not known; wires that end beside it: In, Out2[4]
  // IsEqual #(.generic("value := 67;")) isequal_25: pin names not known; wires that end beside it: In, Out2[3]
  // IsEqual #(.generic("value := 66;")) isequal_26: pin names not known; wires that end beside it: In, Out2[2]
  // IsEqual #(.generic("value := 65;")) isequal_27: pin names not known; wires that end beside it: In, Out2[1]
  // IsEqual #(.generic("value := 64;")) isequal_28: pin names not known; wires that end beside it: In, Out2[0]
  // IsEqual #(.generic("value := 63;")) isequal_29: pin names not known; wires that end beside it: In, Out1[63]
  // IsEqual #(.generic("value := 62;")) isequal_30: pin names not known; wires that end beside it: In, Out1[62]
  // IsEqual #(.generic("value := 61;")) isequal_31: pin names not known; wires that end beside it: In, Out1[61]
  // IsEqual #(.generic("value := 60;")) isequal_32: pin names not known; wires that end beside it: In, Out1[60]
  // IsEqual #(.generic("value := 59;")) isequal_33: pin names not known; wires that end beside it: In, Out1[59]
  // IsEqual #(.generic("value := 58;")) isequal_34: pin names not known; wires that end beside it: In, Out1[58]
  // IsEqual #(.generic("value := 57;")) isequal_35: pin names not known; wires that end beside it: In, Out1[57]
  // IsEqual #(.generic("value := 56;")) isequal_36: pin names not known; wires that end beside it: In, Out1[56]
  // IsEqual #(.generic("value := 55;")) isequal_37: pin names not known; wires that end beside it: In, Out1[55]
  // IsEqual #(.generic("value := 54;")) isequal_38: pin names not known; wires that end beside it: In, Out1[54]
  // IsEqual #(.generic("value := 53;")) isequal_39: pin names not known; wires that end beside it: In, Out1[53]
  // IsEqual #(.generic("value := 52;")) isequal_40: pin names not known; wires that end beside it: In, Out1[52]
  // IsEqual #(.generic("value := 51;")) isequal_41: pin names not known; wires that end beside it: In, Out1[51]
  // IsEqual #(.generic("value := 50;")) isequal_42: pin names not known; wires that end beside it: In, Out1[50]
  // IsEqual #(.generic("value := 49;")) isequal_43: pin names not known; wires that end beside it: In, Out1[49]
  // IsEqual #(.generic("value := 48;")) isequal_44: pin names not known; wires that end beside it: In, Out1[48]
  // IsEqual #(.generic("value := 47;")) isequal_45: pin names not known; wires that end beside it: In, Out1[47]
  // IsEqual #(.generic("value := 46;")) isequal_46: pin names not known; wires that end beside it: In, Out1[46]
  // IsEqual #(.generic("value := 45;")) isequal_47: pin names not known; wires that end beside it: In, Out1[45]
  // IsEqual #(.generic("value := 44;")) isequal_48: pin names not known; wires that end beside it: In, Out1[44]
  // IsEqual #(.generic("value := 43;")) isequal_49: pin names not known; wires that end beside it: In, Out1[43]
  // IsEqual #(.generic("value := 42;")) isequal_50: pin names not known; wires that end beside it: In, Out1[42]
  // IsEqual #(.generic("value := 41;")) isequal_51: pin names not known; wires that end beside it: In, Out1[41]
  // IsEqual #(.generic("value := 40;")) isequal_52: pin names not known; wires that end beside it: In, Out1[40]
  // IsEqual #(.generic("value := 39;")) isequal_53: pin names not known; wires that end beside it: In, Out1[39]
  // IsEqual #(.generic("value := 38;")) isequal_54: pin names not known; wires that end beside it: In, Out1[38]
  // IsEqual #(.generic("value := 37;")) isequal_55: pin names not known; wires that end beside it: In, Out1[37]
  // IsEqual #(.generic("value := 36;")) isequal_56: pin names not known; wires that end beside it: In, Out1[36]
  // IsEqual #(.generic("value := 35;")) isequal_57: pin names not known; wires that end beside it: In, Out1[35]
  // IsEqual #(.generic("value := 34;")) isequal_58: pin names not known; wires that end beside it: In, Out1[34]
  // IsEqual #(.generic("value := 33;")) isequal_59: pin names not known; wires that end beside it: In, Out1[33]
  // IsEqual #(.generic("value := 32;")) isequal_60: pin names not known; wires that end beside it: In, Out1[32]
  // IsEqual #(.generic("value := 31;")) isequal_61: pin names not known; wires that end beside it: In, Out1[31]
  // IsEqual #(.generic("value := 30;")) isequal_62: pin names not known; wires that end beside it: In, Out1[30]
  // IsEqual #(.generic("value := 29;")) isequal_63: pin names not known; wires that end beside it: In, Out1[29]
  // IsEqual #(.generic("value := 28;")) isequal_64: pin names not known; wires that end beside it: In, Out1[28]
  // IsEqual #(.generic("value := 27;")) isequal_65: pin names not known; wires that end beside it: In, Out1[27]
  // IsEqual #(.generic("value := 26;")) isequal_66: pin names not known; wires that end beside it: In, Out1[26]
  // IsEqual #(.generic("value := 25;")) isequal_67: pin names not known; wires that end beside it: In, Out1[25]
  // IsEqual #(.generic("value := 24;")) isequal_68: pin names not known; wires that end beside it: In, Out1[24]
  // IsEqual #(.generic("value := 23;")) isequal_69: pin names not known; wires that end beside it: In, Out1[23]
  // IsEqual #(.generic("value := 22;")) isequal_70: pin names not known; wires that end beside it: In, Out1[22]
  // IsEqual #(.generic("value := 21;")) isequal_71: pin names not known; wires that end beside it: In, Out1[21]
  // IsEqual #(.generic("value := 20;")) isequal_72: pin names not known; wires that end beside it: In, Out1[20]
  // IsEqual #(.generic("value := 19;")) isequal_73: pin names not known; wires that end beside it: In, Out1[19]
  // IsEqual #(.generic("value := 18;")) isequal_74: pin names not known; wires that end beside it: In, Out1[18]
  // IsEqual #(.generic("value := 17;")) isequal_75: pin names not known; wires that end beside it: In, Out1[17]
  // IsEqual #(.generic("value := 16;")) isequal_76: pin names not known; wires that end beside it: In, Out1[16]
  // IsEqual #(.generic("value := 15;")) isequal_77: pin names not known; wires that end beside it: In, Out1[15]
  // IsEqual #(.generic("value := 14;")) isequal_78: pin names not known; wires that end beside it: In, Out1[14]
  // IsEqual #(.generic("value := 13;")) isequal_79: pin names not known; wires that end beside it: In, Out1[13]
  // IsEqual #(.generic("value := 12;")) isequal_80: pin names not known; wires that end beside it: In, Out1[12]
  // IsEqual #(.generic("value := 11;")) isequal_81: pin names not known; wires that end beside it: In, Out1[11]
  // IsEqual #(.generic("value := 10;")) isequal_82: pin names not known; wires that end beside it: In, Out1[10]
  // IsEqual #(.generic("value := 9;")) isequal_83: pin names not known; wires that end beside it: In, Out1[9]
  // IsEqual #(.generic("value := 8;")) isequal_84: pin names not known; wires that end beside it: In, Out1[8]
  // IsEqual #(.generic("value := 7;")) isequal_85: pin names not known; wires that end beside it: In, Out1[7]
  // IsEqual #(.generic("value := 6;")) isequal_86: pin names not known; wires that end beside it: In, Out1[6]
  // IsEqual #(.generic("value := 5;")) isequal_87: pin names not known; wires that end beside it: In, Out1[5]
  // IsEqual #(.generic("value := 4;")) isequal_88: pin names not known; wires that end beside it: In, Out1[4]
  // IsEqual #(.generic("value := 3;")) isequal_89: pin names not known; wires that end beside it: In, Out1[3]
  // IsEqual #(.generic("value := 2;")) isequal_90: pin names not known; wires that end beside it: In, Out1[2]
  // IsEqual #(.generic("value := 1;")) isequal_91: pin names not known; wires that end beside it: In, Out1[1]
  // IsEqual #(.generic("value := 0;")) isequal_92: pin names not known; wires that end beside it: In, Out1[0]
endmodule
