// Digital circuit GetRegisters.dig as structural Verilog
module GetRegisters (
  input  [31:0] R1,
  input  [4:0] R2,
  input  [4:0] R3,
  input  [31:0] RD,
  input  SetD,
  input  [31:0] Data,
  output [31:0] Out1,
  output [31:0] Out2,
  output [31:0] Out3
);

  wire [31:0] cor_1_out, cor_2_out, cor_3_out, cor_4_out, cor_5_out, cor_6_out, cor_7_out, cor_8_out,
       cor_9_out, cor_10_out, cor_11_out, cor_12_out, cor_13_out, cor_14_out, cor_15_out, cor_16_out,
       cor_17_out, cor_18_out, cor_19_out, cor_20_out, cor_21_out, cor_22_out, cor_23_out, cor_24_out,
       cor_25_out, cor_26_out, cor_27_out, cor_28_out, cor_29_out, cor_30_out, cor_31_out, cor_33_out,
       cor_34_out, cor_35_out, cor_36_out, cor_37_out, cor_38_out, cor_39_out, cor_40_out, cor_41_out,
       cor_42_out, cor_43_out, cor_44_out, cor_45_out, cor_46_out, cor_47_out, cor_48_out, cor_49_out,
       cor_50_out, cor_51_out, cor_52_out, cor_53_out, cor_54_out, cor_55_out, cor_56_out, cor_57_out,
       cor_58_out, cor_59_out, cor_60_out, cor_61_out, cor_62_out, cor_63_out, cor_65_out, cor_66_out,
       cor_67_out, cor_68_out, cor_69_out, cor_70_out, cor_71_out, cor_72_out, cor_73_out, cor_74_out,
       cor_75_out, cor_76_out, cor_77_out, cor_78_out, cor_79_out, cor_80_out, cor_81_out, cor_82_out,
       cor_83_out, cor_84_out, cor_85_out, cor_86_out, cor_87_out, cor_88_out, cor_89_out, cor_90_out,
       cor_91_out, cor_92_out, cor_93_out, cor_94_out, cor_95_out, register_1_out, register_2_out,
       register_3_out, register_4_out, register_5_out, register_6_out, register_7_out, register_8_out,
       register_9_out, register_10_out, register_11_out, register_12_out, register_13_out, register_14_out,
       register_15_out, register_16_out, register_17_out, register_18_out, register_19_out, register_20_out,
       register_21_out, register_22_out, register_23_out, register_24_out, register_25_out, register_26_out,
       register_27_out, register_28_out, register_29_out, register_30_out, register_31_out, register_32_out,
       shiftleft_1_out, shiftleft_2_out, shiftleft_3_out, shiftleft_4_out;

  ShiftLeft shiftleft_1 (.A(32'h1), .B({{27{1'b0}}, R1[4:0]}), .Out(shiftleft_1_out));
  ShiftLeft shiftleft_2 (.A(32'h1), .B({{27{1'b0}}, R2}), .Out(shiftleft_2_out));
  ShiftLeft shiftleft_3 (.A(32'h1), .B({{27{1'b0}}, R3}), .Out(shiftleft_3_out));
  ShiftLeft shiftleft_4 (.A({{31{1'b0}}, SetD}), .B({{27{1'b0}}, RD[4:0]}), .Out(shiftleft_4_out));
  Register register_1 (.Data(Data), .Str(shiftleft_4_out[31]), .Out(register_1_out));
  Register register_2 (.Data(Data), .Str(shiftleft_4_out[30]), .Out(register_2_out));
  Register register_3 (.Data(Data), .Str(shiftleft_4_out[29]), .Out(register_3_out));
  Register register_4 (.Data(Data), .Str(shiftleft_4_out[28]), .Out(register_4_out));
  Register register_5 (.Data(Data), .Str(shiftleft_4_out[27]), .Out(register_5_out));
  Register register_6 (.Data(Data), .Str(shiftleft_4_out[26]), .Out(register_6_out));
  Register register_7 (.Data(Data), .Str(shiftleft_4_out[25]), .Out(register_7_out));
  Register register_8 (.Data(Data), .Str(shiftleft_4_out[24]), .Out(register_8_out));
  Register register_9 (.Data(Data), .Str(shiftleft_4_out[23]), .Out(register_9_out));
  Register register_10 (.Data(Data), .Str(shiftleft_4_out[22]), .Out(register_10_out));
  Register register_11 (.Data(Data), .Str(shiftleft_4_out[21]), .Out(register_11_out));
  Register register_12 (.Data(Data), .Str(shiftleft_4_out[20]), .Out(register_12_out));
  Register register_13 (.Data(Data), .Str(shiftleft_4_out[19]), .Out(register_13_out));
  Register register_14 (.Data(Data), .Str(shiftleft_4_out[18]), .Out(register_14_out));
  Register register_15 (.Data(Data), .Str(shiftleft_4_out[17]), .Out(register_15_out));
  Register register_16 (.Data(Data), .Str(shiftleft_4_out[16]), .Out(register_16_out));
  Register register_17 (.Data(Data), .Str(shiftleft_4_out[15]), .Out(register_17_out));
  Register register_18 (.Data(Data), .Str(shiftleft_4_out[14]), .Out(register_18_out));
  Register register_19 (.Data(Data), .Str(shiftleft_4_out[13]), .Out(register_19_out));
  Register register_20 (.Data(Data), .Str(shiftleft_4_out[12]), .Out(register_20_out));
  Register register_21 (.Data(Data), .Str(shiftleft_4_out[11]), .Out(register_21_out));
  Register register_22 (.Data(Data), .Str(shiftleft_4_out[10]), .Out(register_22_out));
  Register register_23 (.Data(Data), .Str(shiftleft_4_out[9]), .Out(register_23_out));
  Register register_24 (.Data(Data), .Str(shiftleft_4_out[8]), .Out(register_24_out));
  Register register_25 (.Data(Data), .Str(shiftleft_4_out[7]), .Out(register_25_out));
  Register register_26 (.Data(Data), .Str(shiftleft_4_out[6]), .Out(register_26_out));
  Register register_27 (.Data(Data), .Str(shiftleft_4_out[5]), .Out(register_27_out));
  Register register_28 (.Data(Data), .Str(shiftleft_4_out[4]), .Out(register_28_out));
  Register register_29 (.Data(Data), .Str(shiftleft_4_out[3]), .Out(register_29_out));
  Register register_30 (.Data(Data), .Str(shiftleft_4_out[2]), .Out(register_30_out));
  Register register_31 (.Data(Data), .Str(shiftleft_4_out[1]), .Out(register_31_out));
  Register register_32 (.Data(Data), .Str(shiftleft_4_out[0]), .Out(register_32_out));
  COr cor_1 (.In1({32{1'b0}}), .In2(register_1_out), .Set(shiftleft_3_out[31]), .Out(cor_1_out));
  COr cor_2 (.In1(cor_1_out), .In2(register_2_out), .Set(shiftleft_3_out[30]), .Out(cor_2_out));
  COr cor_3 (.In1(cor_2_out), .In2(register_3_out), .Set(shiftleft_3_out[29]), .Out(cor_3_out));
  COr cor_4 (.In1(cor_3_out), .In2(register_4_out), .Set(shiftleft_3_out[28]), .Out(cor_4_out));
  COr cor_5 (.In1(cor_4_out), .In2(register_5_out), .Set(shiftleft_3_out[27]), .Out(cor_5_out));
  COr cor_6 (.In1(cor_5_out), .In2(register_6_out), .Set(shiftleft_3_out[26]), .Out(cor_6_out));
  COr cor_7 (.In1(cor_6_out), .In2(register_7_out), .Set(shiftleft_3_out[25]), .Out(cor_7_out));
  COr cor_8 (.In1(cor_7_out), .In2(register_8_out), .Set(shiftleft_3_out[24]), .Out(cor_8_out));
  COr cor_9 (.In1(cor_8_out), .In2(register_9_out), .Set(shiftleft_3_out[23]), .Out(cor_9_out));
  COr cor_10 (.In1(cor_9_out), .In2(register_10_out), .Set(shiftleft_3_out[22]), .Out(cor_10_out));
  COr cor_11 (.In1(cor_10_out), .In2(register_11_out), .Set(shiftleft_3_out[21]), .Out(cor_11_out));
  COr cor_12 (.In1(cor_11_out), .In2(register_12_out), .Set(shiftleft_3_out[20]), .Out(cor_12_out));
  COr cor_13 (.In1(cor_12_out), .In2(register_13_out), .Set(shiftleft_3_out[19]), .Out(cor_13_out));
  COr cor_14 (.In1(cor_13_out), .In2(register_14_out), .Set(shiftleft_3_out[18]), .Out(cor_14_out));
  COr cor_15 (.In1(cor_14_out), .In2(register_15_out), .Set(shiftleft_3_out[17]), .Out(cor_15_out));
  COr cor_16 (.In1(cor_15_out), .In2(register_16_out), .Set(shiftleft_3_out[16]), .Out(cor_16_out));
  COr cor_17 (.In1(cor_16_out), .In2(register_17_out), .Set(shiftleft_3_out[15]), .Out(cor_17_out));
  COr cor_18 (.In1(cor_17_out), .In2(register_18_out), .Set(shiftleft_3_out[14]), .Out(cor_18_out));
  COr cor_19 (.In1(cor_18_out), .In2(register_19_out), .Set(shiftleft_3_out[13]), .Out(cor_19_out));
  COr cor_20 (.In1(cor_19_out), .In2(register_20_out), .Set(shiftleft_3_out[12]), .Out(cor_20_out));
  COr cor_21 (.In1(cor_20_out), .In2(register_21_out), .Set(shiftleft_3_out[11]), .Out(cor_21_out));
  COr cor_22 (.In1(cor_21_out), .In2(register_22_out), .Set(shiftleft_3_out[10]), .Out(cor_22_out));
  COr cor_23 (.In1(cor_22_out), .In2(register_23_out), .Set(shiftleft_3_out[9]), .Out(cor_23_out));
  COr cor_24 (.In1(cor_23_out), .In2(register_24_out), .Set(shiftleft_3_out[8]), .Out(cor_24_out));
  COr cor_25 (.In1(cor_24_out), .In2(register_25_out), .Set(shiftleft_3_out[7]), .Out(cor_25_out));
  COr cor_26 (.In1(cor_25_out), .In2(register_26_out), .Set(shiftleft_3_out[6]), .Out(cor_26_out));
  COr cor_27 (.In1(cor_26_out), .In2(register_27_out), .Set(shiftleft_3_out[5]), .Out(cor_27_out));
  COr cor_28 (.In1(cor_27_out), .In2(register_28_out), .Set(shiftleft_3_out[4]), .Out(cor_28_out));
  COr cor_29 (.In1(cor_28_out), .In2(register_29_out), .Set(shiftleft_3_out[3]), .Out(cor_29_out));
  COr cor_30 (.In1(cor_29_out), .In2(register_30_out), .Set(shiftleft_3_out[2]), .Out(cor_30_out));
  COr cor_31 (.In1(cor_30_out), .In2(register_31_out), .Set(shiftleft_3_out[1]), .Out(cor_31_out));
  COr cor_32 (.In1(cor_31_out), .In2(register_32_out), .Set(shiftleft_3_out[0]), .Out(Out3));
  COr cor_33 (.In1({32{1'b0}}), .In2(register_1_out), .Set(shiftleft_2_out[31]), .Out(cor_33_out));
  COr cor_34 (.In1(cor_33_out), .In2(register_2_out), .Set(shiftleft_2_out[30]), .Out(cor_34_out));
  COr cor_35 (.In1(cor_34_out), .In2(register_3_out), .Set(shiftleft_2_out[29]), .Out(cor_35_out));
  COr cor_36 (.In1(cor_35_out), .In2(register_4_out), .Set(shiftleft_2_out[28]), .Out(cor_36_out));
  COr cor_37 (.In1(cor_36_out), .In2(register_5_out), .Set(shiftleft_2_out[27]), .Out(cor_37_out));
  COr cor_38 (.In1(cor_37_out), .In2(register_6_out), .Set(shiftleft_2_out[26]), .Out(cor_38_out));
  COr cor_39 (.In1(cor_38_out), .In2(register_7_out), .Set(shiftleft_2_out[25]), .Out(cor_39_out));
  COr cor_40 (.In1(cor_39_out), .In2(register_8_out), .Set(shiftleft_2_out[24]), .Out(cor_40_out));
  COr cor_41 (.In1(cor_40_out), .In2(register_9_out), .Set(shiftleft_2_out[23]), .Out(cor_41_out));
  COr cor_42 (.In1(cor_41_out), .In2(register_10_out), .Set(shiftleft_2_out[22]), .Out(cor_42_out));
  COr cor_43 (.In1(cor_42_out), .In2(register_11_out), .Set(shiftleft_2_out[21]), .Out(cor_43_out));
  COr cor_44 (.In1(cor_43_out), .In2(register_12_out), .Set(shiftleft_2_out[20]), .Out(cor_44_out));
  COr cor_45 (.In1(cor_44_out), .In2(register_13_out), .Set(shiftleft_2_out[19]), .Out(cor_45_out));
  COr cor_46 (.In1(cor_45_out), .In2(register_14_out), .Set(shiftleft_2_out[18]), .Out(cor_46_out));
  COr cor_47 (.In1(cor_46_out), .In2(register_15_out), .Set(shiftleft_2_out[17]), .Out(cor_47_out));
  COr cor_48 (.In1(cor_47_out), .In2(register_16_out), .Set(shiftleft_2_out[16]), .Out(cor_48_out));
  COr cor_49 (.In1(cor_48_out), .In2(register_17_out), .Set(shiftleft_2_out[15]), .Out(cor_49_out));
  COr cor_50 (.In1(cor_49_out), .In2(register_18_out), .Set(shiftleft_2_out[14]), .Out(cor_50_out));
  COr cor_51 (.In1(cor_50_out), .In2(register_19_out), .Set(shiftleft_2_out[13]), .Out(cor_51_out));
  COr cor_52 (.In1(cor_51_out), .In2(register_20_out), .Set(shiftleft_2_out[12]), .Out(cor_52_out));
  COr cor_53 (.In1(cor_52_out), .In2(register_21_out), .Set(shiftleft_2_out[11]), .Out(cor_53_out));
  COr cor_54 (.In1(cor_53_out), .In2(register_22_out), .Set(shiftleft_2_out[10]), .Out(cor_54_out));
  COr cor_55 (.In1(cor_54_out), .In2(register_23_out), .Set(shiftleft_2_out[9]), .Out(cor_55_out));
  COr cor_56 (.In1(cor_55_out), .In2(register_24_out), .Set(shiftleft_2_out[8]), .Out(cor_56_out));
  COr cor_57 (.In1(cor_56_out), .In2(register_25_out), .Set(shiftleft_2_out[7]), .Out(cor_57_out));
  COr cor_58 (.In1(cor_57_out), .In2(register_26_out), .Set(shiftleft_2_out[6]), .Out(cor_58_out));
  COr cor_59 (.In1(cor_58_out), .In2(register_27_out), .Set(shiftleft_2_out[5]), .Out(cor_59_out));
  COr cor_60 (.In1(cor_59_out), .In2(register_28_out), .Set(shiftleft_2_out[4]), .Out(cor_60_out));
  COr cor_61 (.In1(cor_60_out), .In2(register_29_out), .Set(shiftleft_2_out[3]), .Out(cor_61_out));
  COr cor_62 (.In1(cor_61_out), .In2(register_30_out), .Set(shiftleft_2_out[2]), .Out(cor_62_out));
  COr cor_63 (.In1(cor_62_out), .In2(register_31_out), .Set(shiftleft_2_out[1]), .Out(cor_63_out));
  COr cor_64 (.In1(cor_63_out), .In2(register_32_out), .Set(shiftleft_2_out[0]), .Out(Out2));
  COr cor_65 (.In1({32{1'b0}}), .In2(register_1_out), .Set(shiftleft_1_out[31]), .Out(cor_65_out));
  COr cor_66 (.In1(cor_65_out), .In2(register_2_out), .Set(shiftleft_1_out[30]), .Out(cor_66_out));
  COr cor_67 (.In1(cor_66_out), .In2(register_3_out), .Set(shiftleft_1_out[29]), .Out(cor_67_out));
  COr cor_68 (.In1(cor_67_out), .In2(register_4_out), .Set(shiftleft_1_out[28]), .Out(cor_68_out));
  COr cor_69 (.In1(cor_68_out), .In2(register_5_out), .Set(shiftleft_1_out[27]), .Out(cor_69_out));
  COr cor_70 (.In1(cor_69_out), .In2(register_6_out), .Set(shiftleft_1_out[26]), .Out(cor_70_out));
  COr cor_71 (.In1(cor_70_out), .In2(register_7_out), .Set(shiftleft_1_out[25]), .Out(cor_71_out));
  COr cor_72 (.In1(cor_71_out), .In2(register_8_out), .Set(shiftleft_1_out[24]), .Out(cor_72_out));
  COr cor_73 (.In1(cor_72_out), .In2(register_9_out), .Set(shiftleft_1_out[23]), .Out(cor_73_out));
  COr cor_74 (.In1(cor_73_out), .In2(register_10_out), .Set(shiftleft_1_out[22]), .Out(cor_74_out));
  COr cor_75 (.In1(cor_74_out), .In2(register_11_out), .Set(shiftleft_1_out[21]), .Out(cor_75_out));
  COr cor_76 (.In1(cor_75_out), .In2(register_12_out), .Set(shiftleft_1_out[20]), .Out(cor_76_out));
  COr cor_77 (.In1(cor_76_out), .In2(register_13_out), .Set(shiftleft_1_out[19]), .Out(cor_77_out));
  COr cor_78 (.In1(cor_77_out), .In2(register_14_out), .Set(shiftleft_1_out[18]), .Out(cor_78_out));
  COr cor_79 (.In1(cor_78_out), .In2(register_15_out), .Set(shiftleft_1_out[17]), .Out(cor_79_out));
  COr cor_80 (.In1(cor_79_out), .In2(register_16_out), .Set(shiftleft_1_out[16]), .Out(cor_80_out));
  COr cor_81 (.In1(cor_80_out), .In2(register_17_out), .Set(shiftleft_1_out[15]), .Out(cor_81_out));
  COr cor_82 (.In1(cor_81_out), .In2(register_18_out), .Set(shiftleft_1_out[14]), .Out(cor_82_out));
  COr cor_83 (.In1(cor_82_out), .In2(register_19_out), .Set(shiftleft_1_out[13]), .Out(cor_83_out));
  COr cor_84 (.In1(cor_83_out), .In2(register_20_out), .Set(shiftleft_1_out[12]), .Out(cor_84_out));
  COr cor_85 (.In1(cor_84_out), .In2(register_21_out), .Set(shiftleft_1_out[11]), .Out(cor_85_out));
  COr cor_86 (.In1(cor_85_out), .In2(register_22_out), .Set(shiftleft_1_out[10]), .Out(cor_86_out));
  COr cor_87 (.In1(cor_86_out), .In2(register_23_out), .Set(shiftleft_1_out[9]), .Out(cor_87_out));
  COr cor_88 (.In1(cor_87_out), .In2(register_24_out), .Set(shiftleft_1_out[8]), .Out(cor_88_out));
  COr cor_89 (.In1(cor_88_out), .In2(register_25_out), .Set(shiftleft_1_out[7]), .Out(cor_89_out));
  COr cor_90 (.In1(cor_89_out), .In2(register_26_out), .Set(shiftleft_1_out[6]), .Out(cor_90_out));
  COr cor_91 (.In1(cor_90_out), .In2(register_27_out), .Set(shiftleft_1_out[5]), .Out(cor_91_out));
  COr cor_92 (.In1(cor_91_out), .In2(register_28_out), .Set(shiftleft_1_out[4]), .Out(cor_92_out));
  COr cor_93 (.In1(cor_92_out), .In2(register_29_out), .Set(shiftleft_1_out[3]), .Out(cor_93_out));
  COr cor_94 (.In1(cor_93_out), .In2(register_30_out), .Set(shiftleft_1_out[2]), .Out(cor_94_out));
  COr cor_95 (.In1(cor_94_out), .In2(register_31_out), .Set(shiftleft_1_out[1]), .Out(cor_95_out));
  COr cor_96 (.In1(cor_95_out), .In2(register_32_out), .Set(shiftleft_1_out[0]), .Out(Out1));
  // Pins of 5 and 32 bits meet at R1
  // Pins of 5 and 32 bits meet at RD
endmodule
