// Digital circuit COr.dig as structural Verilog
module COr (
  input  [31:0] In1,
  input  [31:0] In2,
  input  Set,
  output [31:0] Out
);

  wire [31:0] and_1_out, span32_1_out;

  Span32 span32_1 (.In(Set), .Out(span32_1_out));
  assign and_1_out = In2 & span32_1_out;  // And and_1, 32 bits wide
  assign Out = In1 | and_1_out;  // Or or_1, 32 bits wide
endmodule
