// Digital circuit RegisterBit.dig as structural Verilog
module RegisterBit (
  input  Data,
  input  Str,
  output Out
);

  wire and_1_out, and_2_out, not_1_out;

  not not_1 (not_1_out, Data);
  and and_1 (and_1_out, Str, Data);
  and and_2 (and_2_out, not_1_out, Str);
  RS_FF_AS rs_ff_as_1 (.S(and_1_out), .R(and_2_out), .Q(Out));  // open: nQ
endmodule
