// Digital circuit Register.dig as structural Verilog
module Register (
  input  [31:0] Data,
  input  Str,
  output [31:0] Out
);

  RegisterBit registerbit_1 (.Data(Data[31]), .Str(Str), .Out(Out[31]));
  RegisterBit registerbit_2 (.Data(Data[30]), .Str(Str), .Out(Out[30]));
  RegisterBit registerbit_3 (.Data(Data[29]), .Str(Str), .Out(Out[29]));
  RegisterBit registerbit_4 (.Data(Data[28]), .Str(Str), .Out(Out[28]));
  RegisterBit registerbit_5 (.Data(Data[27]), .Str(Str), .Out(Out[27]));
  RegisterBit registerbit_6 (.Data(Data[26]), .Str(Str), .Out(Out[26]));
  RegisterBit registerbit_7 (.Data(Data[25]), .Str(Str), .Out(Out[25]));
  RegisterBit registerbit_8 (.Data(Data[24]), .Str(Str), .Out(Out[24]));
  RegisterBit registerbit_9 (.Data(Data[23]), .Str(Str), .Out(Out[23]));
  RegisterBit registerbit_10 (.Data(Data[22]), .Str(Str), .Out(Out[22]));
  RegisterBit registerbit_11 (.Data(Data[21]), .Str(Str), .Out(Out[21]));
  RegisterBit registerbit_12 (.Data(Data[20]), .Str(Str), .Out(Out[20]));
  RegisterBit registerbit_13 (.Data(Data[19]), .Str(Str), .Out(Out[19]));
  RegisterBit registerbit_14 (.Data(Data[18]), .Str(Str), .Out(Out[18]));
  RegisterBit registerbit_15 (.Data(Data[17]), .Str(Str), .Out(Out[17]));
  RegisterBit registerbit_16 (.Data(Data[16]), .Str(Str), .Out(Out[16]));
  RegisterBit registerbit_17 (.Data(Data[15]), .Str(Str), .Out(Out[15]));
  RegisterBit registerbit_18 (.Data(Data[14]), .Str(Str), .Out(Out[14]));
  RegisterBit registerbit_19 (.Data(Data[13]), .Str(Str), .Out(Out[13]));
  RegisterBit registerbit_20 (.Data(Data[12]), .Str(Str), .Out(Out[12]));
  RegisterBit registerbit_21 (.Data(Data[11]), .Str(Str), .Out(Out[11]));
  RegisterBit registerbit_22 (.Data(Data[10]), .Str(Str), .Out(Out[10]));
  RegisterBit registerbit_23 (.Data(Data[9]), .Str(Str), .Out(Out[9]));
  RegisterBit registerbit_24 (.Data(Data[8]), .Str(Str), .Out(Out[8]));
  RegisterBit registerbit_25 (.Data(Data[7]), .Str(Str), .Out(Out[7]));
  RegisterBit registerbit_26 (.Data(Data[6]), .Str(Str), .Out(Out[6]));
  RegisterBit registerbit_27 (.Data(Data[5]), .Str(Str), .Out(Out[5]));
  RegisterBit registerbit_28 (.Data(Data[4]), .Str(Str), .Out(Out[4]));
  RegisterBit registerbit_29 (.Data(Data[3]), .Str(Str), .Out(Out[3]));
  RegisterBit registerbit_30 (.Data(Data[2]), .Str(Str), .Out(Out[2]));
  RegisterBit registerbit_31 (.Data(Data[1]), .Str(Str), .Out(Out[1]));
  RegisterBit registerbit_32 (.Data(Data[0]), .Str(Str), .Out(Out[0]));
endmodule
