// Digital circuit Board.dig as structural Verilog
module Board (
  input  clk
);

  wire processor_1_readrom, processor_1_statea_2, processor_1_stateb_2, processor_1_useregister_2,
       processor_1_writetoram;
  wire [15:0] processor_1_romaddr;
  wire [23:0] processor_1_ramaddr;
  wire [31:0] blockramdualport_1_d, processor_1_ramin, rom_1_d;

  GraphicCard #(.Bits(16)) graphiccard_1 ();  // open: A, str, C, ld, B, D
  Processor processor_1 (
    .StateA(processor_1_statea_2), .StateB(processor_1_stateb_2), .ReadRam(clk), .RomOut(rom_1_d),
    .RamOut(blockramdualport_1_d), .UseRegister(processor_1_useregister_2), .StateA_2(processor_1_statea_2),
    .StateB_2(processor_1_stateb_2), .ReadRom(processor_1_readrom), .WriteToRam(processor_1_writetoram),
    .RomAddr(processor_1_romaddr), .RamAddr(processor_1_ramaddr), .RamIn(processor_1_ramin),
    .UseRegister_2(processor_1_useregister_2));
  ROM #(.AddrBits(16), .Bits(32)) rom_1 (.A(processor_1_romaddr), .sel(processor_1_readrom), .D(rom_1_d));
  BlockRAMDualPort #(.AddrBits(24), .Bits(32)) blockramdualport_1 (
    .A(processor_1_ramaddr), .Din(processor_1_ramin), .str(processor_1_writetoram), .C(clk),
    .D(blockramdualport_1_d));
endmodule
