// Digital circuit ConVal.dig as structural Verilog
module ConVal (
  input  [31:0] A,
  input  [31:0] B,
  input  Condition,
  output [31:0] Out
);

  ConBit conbit_1 (.A(A[31]), .B(B[31]), .Condition(Condition), .Out(Out[31]));
  ConBit conbit_2 (.A(A[30]), .B(B[30]), .Condition(Condition), .Out(Out[30]));
  ConBit conbit_3 (.A(A[29]), .B(B[29]), .Condition(Condition), .Out(Out[29]));
  ConBit conbit_4 (.A(A[28]), .B(B[28]), .Condition(Condition), .Out(Out[28]));
  ConBit conbit_5 (.A(A[27]), .B(B[27]), .Condition(Condition), .Out(Out[27]));
  ConBit conbit_6 (.A(A[26]), .B(B[26]), .Condition(Condition), .Out(Out[26]));
  ConBit conbit_7 (.A(A[25]), .B(B[25]), .Condition(Condition), .Out(Out[25]));
  ConBit conbit_8 (.A(A[24]), .B(B[24]), .Condition(Condition), .Out(Out[24]));
  ConBit conbit_9 (.A(A[23]), .B(B[23]), .Condition(Condition), .Out(Out[23]));
  ConBit conbit_10 (.A(A[22]), .B(B[22]), .Condition(Condition), .Out(Out[22]));
  ConBit conbit_11 (.A(A[21]), .B(B[21]), .Condition(Condition), .Out(Out[21]));
  ConBit conbit_12 (.A(A[20]), .B(B[20]), .Condition(Condition), .Out(Out[20]));
  ConBit conbit_13 (.A(A[19]), .B(B[19]), .Condition(Condition), .Out(Out[19]));
  ConBit conbit_14 (.A(A[18]), .B(B[18]), .Condition(Condition), .Out(Out[18]));
  ConBit conbit_15 (.A(A[17]), .B(B[17]), .Condition(Condition), .Out(Out[17]));
  ConBit conbit_16 (.A(A[16]), .B(B[16]), .Condition(Condition), .Out(Out[16]));
  ConBit conbit_17 (.A(A[15]), .B(B[15]), .Condition(Condition), .Out(Out[15]));
  ConBit conbit_18 (.A(A[14]), .B(B[14]), .Condition(Condition), .Out(Out[14]));
  ConBit conbit_19 (.A(A[13]), .B(B[13]), .Condition(Condition), .Out(Out[13]));
  ConBit conbit_20 (.A(A[12]), .B(B[12]), .Condition(Condition), .Out(Out[12]));
  ConBit conbit_21 (.A(A[11]), .B(B[11]), .Condition(Condition), .Out(Out[11]));
  ConBit conbit_22 (.A(A[10]), .B(B[10]), .Condition(Condition), .Out(Out[10]));
  ConBit conbit_23 (.A(A[9]), .B(B[9]), .Condition(Condition), .Out(Out[9]));
  ConBit conbit_24 (.A(A[8]), .B(B[8]), .Condition(Condition), .Out(Out[8]));
  ConBit conbit_25 (.A(A[7]), .B(B[7]), .Condition(Condition), .Out(Out[7]));
  ConBit conbit_26 (.A(A[6]), .B(B[6]), .Condition(Condition), .Out(Out[6]));
  ConBit conbit_27 (.A(A[5]), .B(B[5]), .Condition(Condition), .Out(Out[5]));
  ConBit conbit_28 (.A(A[4]), .B(B[4]), .Condition(Condition), .Out(Out[4]));
  ConBit conbit_29 (.A(A[3]), .B(B[3]), .Condition(Condition), .Out(Out[3]));
  ConBit conbit_30 (.A(A[2]), .B(B[2]), .Condition(Condition), .Out(Out[2]));
  ConBit conbit_31 (.A(A[1]), .B(B[1]), .Condition(Condition), .Out(Out[1]));
  ConBit conbit_32 (.A(A[0]), .B(B[0]), .Condition(Condition), .Out(Out[0]));
endmodule
