// Digital circuit ConBit.dig as structural Verilog
module ConBit (
  input  A,
  input  B,
  input  Condition,
  output Out
);

  wire and_1_out, and_2_out, not_1_out;

  not not_1 (not_1_out, Condition);
  and and_1 (and_1_out, A, not_1_out);
  and and_2 (and_2_out, B, Condition);
  or or_1 (Out, and_1_out, and_2_out);
endmodule
