// Digital circuit NotZero.dig as structural Verilog
module NotZero (
  input  [31:0] In,
  output Out
);

  or or_1 (Out, In[31], In[30], In[29], In[28], In[27], In[26], In[25], In[24], In[23], In[22], In[21], In[20], In[19], In[18], In[17], In[16], In[14], In[13], In[12], In[11], In[10], In[9], In[8], In[7], In[6], In[5], In[4], In[3], In[2], In[1], In[0], In[15]);
endmodule
