// Digital circuit AddInt.dig as structural Verilog
module AddInt (
  input  [31:0] A,
  input  [31:0] B,
  output [31:0] Sum,
  output Overflow
);

  wire addbit_1_cout, addbit_2_cout, addbit_3_cout, addbit_4_cout, addbit_5_cout, addbit_6_cout,
       addbit_7_cout, addbit_8_cout, addbit_9_cout, addbit_10_cout, addbit_11_cout, addbit_12_cout,
       addbit_13_cout, addbit_14_cout, addbit_15_cout, addbit_16_cout, addbit_17_cout, addbit_18_cout,
       addbit_19_cout, addbit_20_cout, addbit_21_cout, addbit_22_cout, addbit_23_cout, addbit_24_cout,
       addbit_25_cout, addbit_26_cout, addbit_27_cout, addbit_28_cout, addbit_29_cout, addbit_30_cout,
       addbit_31_cout;

  AddBit addbit_1 (.A(A[0]), .B(B[0]), .Cin(1'b0), .Sum(Sum[0]), .Cout(addbit_1_cout));
  AddBit addbit_2 (.A(A[1]), .B(B[1]), .Cin(addbit_1_cout), .Sum(Sum[1]), .Cout(addbit_2_cout));
  AddBit addbit_3 (.A(A[2]), .B(B[2]), .Cin(addbit_2_cout), .Sum(Sum[2]), .Cout(addbit_3_cout));
  AddBit addbit_4 (.A(A[3]), .B(B[3]), .Cin(addbit_3_cout), .Sum(Sum[3]), .Cout(addbit_4_cout));
  AddBit addbit_5 (.A(A[4]), .B(B[4]), .Cin(addbit_4_cout), .Sum(Sum[4]), .Cout(addbit_5_cout));
  AddBit addbit_6 (.A(A[5]), .B(B[5]), .Cin(addbit_5_cout), .Sum(Sum[5]), .Cout(addbit_6_cout));
  AddBit addbit_7 (.A(A[6]), .B(B[6]), .Cin(addbit_6_cout), .Sum(Sum[6]), .Cout(addbit_7_cout));
  AddBit addbit_8 (.A(A[7]), .B(B[7]), .Cin(addbit_7_cout), .Sum(Sum[7]), .Cout(addbit_8_cout));
  AddBit addbit_9 (.A(A[8]), .B(B[8]), .Cin(addbit_8_cout), .Sum(Sum[8]), .Cout(addbit_9_cout));
  AddBit addbit_10 (.A(A[9]), .B(B[9]), .Cin(addbit_9_cout), .Sum(Sum[9]), .Cout(addbit_10_cout));
  AddBit addbit_11 (.A(A[10]), .B(B[10]), .Cin(addbit_10_cout), .Sum(Sum[10]), .Cout(addbit_11_cout));
  AddBit addbit_12 (.A(A[11]), .B(B[11]), .Cin(addbit_11_cout), .Sum(Sum[11]), .Cout(addbit_12_cout));
  AddBit addbit_13 (.A(A[12]), .B(B[12]), .Cin(addbit_12_cout), .Sum(Sum[12]), .Cout(addbit_13_cout));
  AddBit addbit_14 (.A(A[13]), .B(B[13]), .Cin(addbit_13_cout), .Sum(Sum[13]), .Cout(addbit_14_cout));
  AddBit addbit_15 (.A(A[14]), .B(B[14]), .Cin(addbit_14_cout), .Sum(Sum[14]), .Cout(addbit_15_cout));
  AddBit addbit_16 (.A(A[15]), .B(B[15]), .Cin(addbit_15_cout), .Sum(Sum[15]), .Cout(addbit_16_cout));
  AddBit addbit_17 (.A(A[16]), .B(B[16]), .Cin(addbit_16_cout), .Sum(Sum[16]), .Cout(addbit_17_cout));
  AddBit addbit_18 (.A(A[17]), .B(B[17]), .Cin(addbit_17_cout), .Sum(Sum[17]), .Cout(addbit_18_cout));
  AddBit addbit_19 (.A(A[18]), .B(B[18]), .Cin(addbit_18_cout), .Sum(Sum[18]), .Cout(addbit_19_cout));
  AddBit addbit_20 (.A(A[19]), .B(B[19]), .Cin(addbit_19_cout), .Sum(Sum[19]), .Cout(addbit_20_cout));
  AddBit addbit_21 (.A(A[20]), .B(B[20]), .Cin(addbit_20_cout), .Sum(Sum[20]), .Cout(addbit_21_cout));
  AddBit addbit_22 (.A(A[21]), .B(B[21]), .Cin(addbit_21_cout), .Sum(Sum[21]), .Cout(addbit_22_cout));
  AddBit addbit_23 (.A(A[22]), .B(B[22]), .Cin(addbit_22_cout), .Sum(Sum[22]), .Cout(addbit_23_cout));
  AddBit addbit_24 (.A(A[23]), .B(B[23]), .Cin(addbit_23_cout), .Sum(Sum[23]), .Cout(addbit_24_cout));
  AddBit addbit_25 (.A(A[24]), .B(B[24]), .Cin(addbit_24_cout), .Sum(Sum[24]), .Cout(addbit_25_cout));
  AddBit addbit_26 (.A(A[25]), .B(B[25]), .Cin(addbit_25_cout), .Sum(Sum[25]), .Cout(addbit_26_cout));
  AddBit addbit_27 (.A(A[26]), .B(B[26]), .Cin(addbit_26_cout), .Sum(Sum[26]), .Cout(addbit_27_cout));
  AddBit addbit_28 (.A(A[27]), .B(B[27]), .Cin(addbit_27_cout), .Sum(Sum[27]), .Cout(addbit_28_cout));
  AddBit addbit_29 (.A(A[28]), .B(B[28]), .Cin(addbit_28_cout), .Sum(Sum[28]), .Cout(addbit_29_cout));
  AddBit addbit_30 (.A(A[29]), .B(B[29]), .Cin(addbit_29_cout), .Sum(Sum[29]), .Cout(addbit_30_cout));
  AddBit addbit_31 (.A(A[30]), .B(B[30]), .Cin(addbit_30_cout), .Sum(Sum[30]), .Cout(addbit_31_cout));
  AddBit addbit_32 (.A(A[31]), .B(B[31]), .Cin(addbit_31_cout), .Sum(Sum[31]), .Cout(Overflow));
endmodule
