// Digital circuit SubBit.dig as structural Verilog
module SubBit (
  input  A,
  input  B,
  input  Cin,
  output Sub,
  output Cout
);

  wire and_1_out, and_2_out, not_1_out, xor_1_out;

  xor xor_1 (xor_1_out, B, Cin);
  and and_1 (and_1_out, B, Cin);
  not not_1 (not_1_out, A);
  xor xor_2 (Sub, A, xor_1_out);
  and and_2 (and_2_out, not_1_out, xor_1_out);
  or or_1 (Cout, and_2_out, and_1_out);
endmodule
