// Digital circuit ShiftLeft.dig as structural Verilog
module ShiftLeft (
  input  [31:0] A,
  input  [31:0] B,
  output [31:0] Out
);

  wire notzero_1_out;
  wire [31:0] conval_1_out, conval_2_out, conval_3_out, conval_4_out, conval_5_out, sl1_1_out, sl2_1_out,
       sl4_1_out, sl8_1_out, sl16_1_out;

  SL16 sl16_1 (.In(conval_2_out), .Out(sl16_1_out));
  SL4 sl4_1 (.In(conval_4_out), .Out(sl4_1_out));
  SL1 sl1_1 (.In(A), .Out(sl1_1_out));
  NotZero notzero_1 (.In({{5{1'b0}}, B[31:5]}), .Out(notzero_1_out));
  ConVal conval_1 (.A(conval_2_out), .B(sl16_1_out), .Condition(B[4]), .Out(conval_1_out));
  ConVal conval_2 (.A(conval_3_out), .B(sl8_1_out), .Condition(B[3]), .Out(conval_2_out));
  ConVal conval_3 (.A(conval_4_out), .B(sl4_1_out), .Condition(B[2]), .Out(conval_3_out));
  ConVal conval_4 (.A(conval_5_out), .B(sl2_1_out), .Condition(B[1]), .Out(conval_4_out));
  ConVal conval_5 (.A(A), .B(sl1_1_out), .Condition(B[0]), .Out(conval_5_out));
  ConVal conval_6 (.A(conval_1_out), .B({32{1'b0}}), .Condition(notzero_1_out), .Out(Out));
  SL8 sl8_1 (.In(conval_3_out), .Out(sl8_1_out));
  SL2 sl2_1 (.In(conval_5_out), .Out(sl2_1_out));
endmodule
