// Digital circuit ShiftRight.dig as structural Verilog
module ShiftRight (
  input  [31:0] A,
  input  [31:0] B,
  output [31:0] Out
);

  wire notzero_1_out;
  wire [31:0] conval_1_out, conval_2_out, conval_3_out, conval_4_out, conval_5_out, sr1_1_out, sr2_1_out,
       sr4_1_out, sr8_1_out, sr16_1_out;

  SR16 sr16_1 (.In(conval_2_out), .Out(sr16_1_out));
  SR4 sr4_1 (.In(conval_4_out), .Out(sr4_1_out));
  SR1 sr1_1 (.In(A), .Out(sr1_1_out));
  NotZero notzero_1 (.In({{5{1'b0}}, B[31:5]}), .Out(notzero_1_out));
  ConVal conval_1 (.A(conval_2_out), .B(sr16_1_out), .Condition(B[4]), .Out(conval_1_out));
  ConVal conval_2 (.A(conval_3_out), .B(sr8_1_out), .Condition(B[3]), .Out(conval_2_out));
  ConVal conval_3 (.A(conval_4_out), .B(sr4_1_out), .Condition(B[2]), .Out(conval_3_out));
  ConVal conval_4 (.A(conval_5_out), .B(sr2_1_out), .Condition(B[1]), .Out(conval_4_out));
  ConVal conval_5 (.A(A), .B(sr1_1_out), .Condition(B[0]), .Out(conval_5_out));
  ConVal conval_6 (.A(conval_1_out), .B({32{1'b0}}), .Condition(notzero_1_out), .Out(Out));
  SR8 sr8_1 (.In(conval_3_out), .Out(sr8_1_out));
  SR2 sr2_1 (.In(conval_5_out), .Out(sr2_1_out));
endmodule
