// Digital circuit SubInt.dig as structural Verilog
module SubInt (
  input  [31:0] A,
  input  [31:0] B,
  output [31:0] Sub,
  output Underflow
);

  wire subbit_1_cout, subbit_2_cout, subbit_3_cout, subbit_4_cout, subbit_5_cout, subbit_6_cout,
       subbit_7_cout, subbit_8_cout, subbit_9_cout, subbit_10_cout, subbit_11_cout, subbit_12_cout,
       subbit_13_cout, subbit_14_cout, subbit_15_cout, subbit_16_cout, subbit_17_cout, subbit_18_cout,
       subbit_19_cout, subbit_20_cout, subbit_21_cout, subbit_22_cout, subbit_23_cout, subbit_24_cout,
       subbit_25_cout, subbit_26_cout, subbit_27_cout, subbit_28_cout, subbit_29_cout, subbit_30_cout,
       subbit_31_cout;

  SubBit subbit_1 (.A(A[0]), .B(B[0]), .Cin(1'b0), .Sub(Sub[0]), .Cout(subbit_1_cout));
  SubBit subbit_2 (.A(A[1]), .B(B[1]), .Cin(subbit_1_cout), .Sub(Sub[1]), .Cout(subbit_2_cout));
  SubBit subbit_3 (.A(A[2]), .B(B[2]), .Cin(subbit_2_cout), .Sub(Sub[2]), .Cout(subbit_3_cout));
  SubBit subbit_4 (.A(A[3]), .B(B[3]), .Cin(subbit_3_cout), .Sub(Sub[3]), .Cout(subbit_4_cout));
  SubBit subbit_5 (.A(A[4]), .B(B[4]), .Cin(subbit_4_cout), .Sub(Sub[4]), .Cout(subbit_5_cout));
  SubBit subbit_6 (.A(A[5]), .B(B[5]), .Cin(subbit_5_cout), .Sub(Sub[5]), .Cout(subbit_6_cout));
  SubBit subbit_7 (.A(A[6]), .B(B[6]), .Cin(subbit_6_cout), .Sub(Sub[6]), .Cout(subbit_7_cout));
  SubBit subbit_8 (.A(A[7]), .B(B[7]), .Cin(subbit_7_cout), .Sub(Sub[7]), .Cout(subbit_8_cout));
  SubBit subbit_9 (.A(A[8]), .B(B[8]), .Cin(subbit_8_cout), .Sub(Sub[8]), .Cout(subbit_9_cout));
  SubBit subbit_10 (.A(A[9]), .B(B[9]), .Cin(subbit_9_cout), .Sub(Sub[9]), .Cout(subbit_10_cout));
  SubBit subbit_11 (.A(A[10]), .B(B[10]), .Cin(subbit_10_cout), .Sub(Sub[10]), .Cout(subbit_11_cout));
  SubBit subbit_12 (.A(A[11]), .B(B[11]), .Cin(subbit_11_cout), .Sub(Sub[11]), .Cout(subbit_12_cout));
  SubBit subbit_13 (.A(A[12]), .B(B[12]), .Cin(subbit_12_cout), .Sub(Sub[12]), .Cout(subbit_13_cout));
  SubBit subbit_14 (.A(A[13]), .B(B[13]), .Cin(subbit_13_cout), .Sub(Sub[13]), .Cout(subbit_14_cout));
  SubBit subbit_15 (.A(A[14]), .B(B[14]), .Cin(subbit_14_cout), .Sub(Sub[14]), .Cout(subbit_15_cout));
  SubBit subbit_16 (.A(A[15]), .B(B[15]), .Cin(subbit_15_cout), .Sub(Sub[15]), .Cout(subbit_16_cout));
  SubBit subbit_17 (.A(A[16]), .B(B[16]), .Cin(subbit_16_cout), .Sub(Sub[16]), .Cout(subbit_17_cout));
  SubBit subbit_18 (.A(A[17]), .B(B[17]), .Cin(subbit_17_cout), .Sub(Sub[17]), .Cout(subbit_18_cout));
  SubBit subbit_19 (.A(A[18]), .B(B[18]), .Cin(subbit_18_cout), .Sub(Sub[18]), .Cout(subbit_19_cout));
  SubBit subbit_20 (.A(A[19]), .B(B[19]), .Cin(subbit_19_cout), .Sub(Sub[19]), .Cout(subbit_20_cout));
  SubBit subbit_21 (.A(A[20]), .B(B[20]), .Cin(subbit_20_cout), .Sub(Sub[20]), .Cout(subbit_21_cout));
  SubBit subbit_22 (.A(A[21]), .B(B[21]), .Cin(subbit_21_cout), .Sub(Sub[21]), .Cout(subbit_22_cout));
  SubBit subbit_23 (.A(A[22]), .B(B[22]), .Cin(subbit_22_cout), .Sub(Sub[22]), .Cout(subbit_23_cout));
  SubBit subbit_24 (.A(A[23]), .B(B[23]), .Cin(subbit_23_cout), .Sub(Sub[23]), .Cout(subbit_24_cout));
  SubBit subbit_25 (.A(A[24]), .B(B[24]), .Cin(subbit_24_cout), .Sub(Sub[24]), .Cout(subbit_25_cout));
  SubBit subbit_26 (.A(A[25]), .B(B[25]), .Cin(subbit_25_cout), .Sub(Sub[25]), .Cout(subbit_26_cout));
  SubBit subbit_27 (.A(A[26]), .B(B[26]), .Cin(subbit_26_cout), .Sub(Sub[26]), .Cout(subbit_27_cout));
  SubBit subbit_28 (.A(A[27]), .B(B[27]), .Cin(subbit_27_cout), .Sub(Sub[27]), .Cout(subbit_28_cout));
  SubBit subbit_29 (.A(A[28]), .B(B[28]), .Cin(subbit_28_cout), .Sub(Sub[28]), .Cout(subbit_29_cout));
  SubBit subbit_30 (.A(A[29]), .B(B[29]), .Cin(subbit_29_cout), .Sub(Sub[29]), .Cout(subbit_30_cout));
  SubBit subbit_31 (.A(A[30]), .B(B[30]), .Cin(subbit_30_cout), .Sub(Sub[30]), .Cout(subbit_31_cout));
  SubBit subbit_32 (.A(A[31]), .B(B[31]), .Cin(subbit_31_cout), .Sub(Sub[31]), .Cout(Underflow));
endmodule
