// Digital circuit Placeholder.dig as structural Verilog
module Placeholder (
);

  GetRegisters getregisters_1 ();  // open: R1, R2, R3, RD, SetD, Data, Out1, Out2, Out3
  AddInt addint_1 ();  // open: A, B, Sum, Overflow
  Register register_1 ();  // open: Data, Str, Out
  SubInt subint_1 ();  // open: A, B, Sub, Underflow
  ShiftLeft shiftleft_1 ();  // open: A, B, Out
  ShiftRight shiftright_1 ();  // open: A, B, Out
endmodule
