// Digital circuit Test.dig as structural Verilog
module Test (
  input  in_1,
  input  [31:0] in_2,
  input  in_3,
  input  [31:0] in_4,
  output [31:0] out_5,
  output [31:0] out_6
);

  Register register_1 (.Data(in_2), .Str(in_1), .Out(out_5));
  Register register_2 (.Data(in_4), .Str(in_3), .Out(out_6));
endmodule
