// Digital circuit Video.dig as structural Verilog
module Video (
  input  [7:0] in_1,
  input  [7:0] in_2,
  input  [7:0] in_3,
  input  clk
);

  wire and_1_out, comparator_1_eq, comparator_2_eq, comparator_3_lt, comparator_4_lt, comparator_5_lt,
       comparator_6_gt, comparator_7_lt, comparator_8_gt, or_1_out, or_2_out;
  wire [7:0] and_3_out, and_4_out, and_5_out;
  wire [7:7] and_2_out;
  wire [9:0] counter_1_out, counter_2_out;

  and and_1 (and_1_out, comparator_2_eq, comparator_1_eq);
  Counter #(.Bits(10)) counter_1 (.en(comparator_2_eq), .C(clk), .clr(and_1_out), .out(counter_1_out));  // open: ovf
  Counter #(.Bits(10)) counter_2 (.en(1'b1), .C(clk), .clr(comparator_2_eq), .out(counter_2_out));  // open: ovf
  Comparator #(.Bits(10)) comparator_1 (.a(counter_1_out), .b(10'h20c), .eq(comparator_1_eq));  // open: gt, lt
  Comparator #(.Bits(10)) comparator_2 (.a(counter_2_out), .b(10'h31f), .eq(comparator_2_eq));  // open: gt, lt
  Comparator #(.Bits(10)) comparator_3 (.a(counter_2_out), .b(10'h280), .lt(comparator_3_lt));  // open: gt, eq
  Comparator #(.Bits(10)) comparator_4 (.a(counter_1_out), .b(10'h1e0), .lt(comparator_4_lt));  // open: gt, eq
  and and_2 (and_2_out[7], comparator_3_lt, comparator_4_lt);
  Comparator #(.Bits(10)) comparator_5 (.a(counter_1_out), .b(10'h1ea), .lt(comparator_5_lt));  // open: gt, eq
  Comparator #(.Bits(10)) comparator_6 (.a(counter_1_out), .b(10'h1eb), .gt(comparator_6_gt));  // open: eq, lt
  Comparator #(.Bits(10)) comparator_7 (.a(counter_2_out), .b(10'h290), .lt(comparator_7_lt));  // open: gt, eq
  Comparator #(.Bits(10)) comparator_8 (.a(counter_2_out), .b(10'h2ef), .gt(comparator_8_gt));  // open: eq, lt
  or or_1 (or_1_out, comparator_5_lt, comparator_6_gt);
  or or_2 (or_2_out, comparator_7_lt, comparator_8_gt);
  assign and_3_out = in_3 & {8{and_2_out[7]}};  // And and_3, 8 bits wide
  assign and_4_out = in_2 & {8{and_2_out[7]}};  // And and_4, 8 bits wide
  assign and_5_out = in_1 & {8{and_2_out[7]}};  // And and_5, 8 bits wide
  VGA vga_1 (.R(and_3_out), .G(and_4_out), .B(and_5_out), .H(or_2_out), .V(or_1_out), .C(clk));

  // Notes on the sheet:
  //   clk: Hz: 131072
endmodule
